# Fritzing sketch Dht22 (saved by Fritzing 0.9.3b)
circuit board: 8.46667cm x 5.64444cm
breadboards: 1

parts:
  Raspberry_Pi_1 = Raspberry Pi 3 [part_number=RPI-3-V1.2]
  Dht1 = Humidity and Temperature Sensor Dht22 or AM2303
  R1 = Resistor [tolerance=±5% resistance=10k package=THT]

nets (from the schematic view):
  N1: Raspberry_Pi_1.GIPO4, Raspberry_Pi_1.GIPO14, Dht1.Data-signal, R1.Pin_0
  N2: Raspberry_Pi_1.GND, Dht1.GND_1
  5V: Raspberry_Pi_1.5V, Dht1.Vcc, R1.Pin_1

custom parts:
  Humidity and Temperature Sensor Dht22 or AM2303: Digital relative humidity & temperature sensor Dht22
